// Logisim project cpu.circ as structural Verilog: 9 circuits, main circuit main
module main (
);

  wire Clk_out, Reset_out;
  wire [1:0] csd_1_mei;
  wire [6:0] csd_1_iri;
  wire [7:0] ar_1_adho, ar_1_adlo, ir_1_do, memory_1_do, pc_1_adho, pc_1_adlo, undriven;
  wire [8:0] csd_1_pce;
  wire [11:0] csd_1_aad;
  wire [12:0] csd_1_sri;
  wire [12:12] csd_1_alo;

  Button Reset (.out(Reset_out));
  Clock Clk (.out(Clk_out));
  AR ar_1 (
    .ADLI(pc_1_adlo), .ADHI(pc_1_adho), .Clk(Clk_out), .Rst(Reset_out), .ADLO(ar_1_adlo), .ADHO(ar_1_adho));  // open: LWE, HWE
  PC pc_1 (
    .Reset(Reset_out), .WE(csd_1_pce[1]), .CE(csd_1_pce[0]), .Clk(Clk_out), .ADLI(pc_1_adlo),
    .ADHI(pc_1_adho), .OE(csd_1_pce[2]), .ADLO(pc_1_adlo), .ADHO(pc_1_adho));
  Memory memory_1 (
    .WE(csd_1_mei[0]), .Clk(Clk_out), .DI(memory_1_do), .ADL(ar_1_adlo), .ADH(ar_1_adho), .OE(csd_1_mei[1]),
    .DO(memory_1_do));
  SP sp_1 (.WE(csd_1_pce[7]), .DI(memory_1_do), .Clk(Clk_out), .Reset(Reset_out), .OE(csd_1_pce[8]), .DO(memory_1_do));
  IR ir_1 (.WE(csd_1_iri[0]), .DI(memory_1_do), .Clk(Clk_out), .Reset(Reset_out), .DO(ir_1_do));
  Registers registers_1 (
    .AWE(csd_1_iri[1]), .XWE(csd_1_iri[3]), .YWE(csd_1_iri[5]), .DBI(memory_1_do), .Clk(Clk_out),
    .Reset(Reset_out), .AO(undriven), .AOE(csd_1_iri[2]), .XOE(csd_1_iri[4]), .YOE(csd_1_iri[6]),
    .DBO(memory_1_do));
  ALU alu_1 (
    .BOr(csd_1_aad[5]), .BXOr(csd_1_aad[6]), .Shl(csd_1_aad[7]), .Shr(csd_1_aad[8]), .BNot(csd_1_aad[9]),
    .Inc(csd_1_aad[10]), .Dec(csd_1_aad[11]), .OE(csd_1_alo[12]), .DBI(memory_1_do), .AI(undriven),
    .Add(csd_1_aad[0]), .Sub(csd_1_aad[1]), .Mul(csd_1_aad[2]), .Div(csd_1_aad[3]), .BAnd(csd_1_aad[4]),
    .DBO(memory_1_do));  // open: C, Z
  CSD csd_1 (
    .Opcode(ir_1_do), .AIO(csd_1_aad[5]), .AXO(csd_1_aad[6]), .ASL(csd_1_aad[7]), .ASR(csd_1_aad[8]),
    .ANO(csd_1_aad[9]), .AIN(csd_1_aad[10]), .ADE(csd_1_aad[11]), .ALO(csd_1_alo[12]), .PCE(csd_1_pce[0]),
    .PCI(csd_1_pce[1]), .PCO(csd_1_pce[2]), .LAI(csd_1_pce[3]), .LAO(csd_1_pce[4]), .HAI(csd_1_pce[5]),
    .HAO(csd_1_pce[6]), .SPI(csd_1_pce[7]), .SPO(csd_1_pce[8]), .MEI(csd_1_mei[0]), .MEO(csd_1_mei[1]),
    .IRI(csd_1_iri[0]), .ARI(csd_1_iri[1]), .ARO(csd_1_iri[2]), .XRI(csd_1_iri[3]), .XRO(csd_1_iri[4]),
    .YRI(csd_1_iri[5]), .YRO(csd_1_iri[6]), .SRI(csd_1_sri[0]), .SRO(csd_1_sri[1]), .RFI(csd_1_sri[2]),
    .CFI(csd_1_sri[3]), .IFS(csd_1_sri[4]), .IFC(csd_1_sri[5]), .HFS(csd_1_sri[6]), .ZFO(csd_1_sri[7]),
    .CFO(csd_1_sri[8]), .EFO(csd_1_sri[9]), .LFO(csd_1_sri[10]), .GFO(csd_1_sri[11]), .IFO(csd_1_sri[12]),
    .AAD(csd_1_aad[0]), .ASU(csd_1_aad[1]), .AMU(csd_1_aad[2]), .ADI(csd_1_aad[3]), .AAN(csd_1_aad[4]));

  // Notes on the sheet:
  //   Opcode
  //   CONTROL SIGNAL DECODER
endmodule

module Memory (
  input  WE,
  input  Clk,
  input  [7:0] DI,
  input  OE,
  input  [7:0] ADL,
  input  [7:0] ADH,
  output [7:0] DO
);

  wire and_1_out, not_1_out, not_2_out;
  wire [7:0] controlled_buffer_1_out, ram_1_dout, rom_1_data;

  not not_1 (not_1_out, ADH[7]);
  RAM #(.addrWidth(15)) ram_1 (
    .addr({ADH[6:0], ADL}), .we(and_1_out), .oe(1'b1), .clk(Clk), .din(DI), .dout(ram_1_dout));
  and and_1 (and_1_out, WE, not_1_out);
  ROM #(.addrWidth(15)) rom_1 (.addr({ADH[6:0], ADL}), .data(rom_1_data));
  assign controlled_buffer_1_out = not_2_out ? ram_1_dout : 8'bz;  // Controlled_Buffer controlled_buffer_1
  not not_2 (not_2_out, ADH[7]);
  assign DO = OE ? controlled_buffer_1_out : 8'bz;  // Controlled_Buffer controlled_buffer_2
  assign controlled_buffer_1_out = ADH[7] ? rom_1_data : 8'bz;  // Controlled_Buffer controlled_buffer_3
endmodule

module PC (
  input  Reset,
  input  WE,
  input  CE,
  input  Clk,
  input  OE,
  input  [7:0] ADLI,
  input  [7:0] ADHI,
  output [7:0] ADLO,
  output [7:0] ADHO
);

  wire [15:0] counter_1_q;

  Counter #(.max('hffff), .width(16)) counter_1 (
    .clr(Reset), .load(WE), .up(1'b1), .count(CE), .clk(Clk), .D({ADHI, ADLI}), .Q(counter_1_q));  // open: carry
  assign {ADHO, ADLO} = OE ? counter_1_q : 16'bz;  // Controlled_Buffer controlled_buffer_1
endmodule

module Registers (
  input  Clk,
  input  Reset,
  input  [7:0] DBI,
  input  [7:0] AO,
  input  AOE,
  input  AWE,
  input  XOE,
  input  XWE,
  input  YOE,
  input  YWE,
  output [7:0] DBO
);

  wire [7:0] register_2_q, register_3_q;

  Register register_1 (.D(DBI), .en(AWE), .clk(Clk), .Q(AO), .clr(Reset));
  Register register_2 (.D(DBI), .en(XWE), .clk(Clk), .Q(register_2_q), .clr(Reset));
  Register register_3 (.D(DBI), .en(YWE), .clk(Clk), .Q(register_3_q), .clr(Reset));
  assign DBO = AOE ? AO : 8'bz;  // Controlled_Buffer controlled_buffer_1
  assign DBO = XOE ? register_2_q : 8'bz;  // Controlled_Buffer controlled_buffer_2
  assign DBO = YOE ? register_3_q : 8'bz;  // Controlled_Buffer controlled_buffer_3
endmodule

module ALU (
  input  Add,
  input  Sub,
  input  Mul,
  input  Div,
  input  BAnd,
  input  BOr,
  input  BXOr,
  input  Shl,
  input  Shr,
  input  BNot,
  input  Inc,
  input  Dec,
  input  [7:0] DBI,
  input  OE,
  input  [7:0] AI,
  output [7:0] DBO,
  output C,
  output Z
);

  wire adder_1_cout, subtractor_1_bout;
  wire [7:0] adder_1_out, adder_2_out, and_2_out, controlled_buffer_1_out, divider_1_out, multiplier_1_cout,
       multiplier_1_out, not_1_out, or_1_out, shifter_1_out, shifter_2_out, subtractor_1_out,
       subtractor_2_out, xor_1_out;

  assign controlled_buffer_1_out = Add ? adder_1_out : 8'bz;  // Controlled_Buffer controlled_buffer_1
  Adder adder_1 (.a(AI), .b(DBI), .out(adder_1_out), .cout(adder_1_cout));  // open: cin
  assign C = Add ? adder_1_cout : 1'bz;  // Controlled_Buffer controlled_buffer_2
  assign controlled_buffer_1_out = Sub ? subtractor_1_out : 8'bz;  // Controlled_Buffer controlled_buffer_3
  Subtractor subtractor_1 (.a(AI), .b(DBI), .out(subtractor_1_out), .bout(subtractor_1_bout));  // open: bin
  assign C = Sub ? subtractor_1_bout : 1'bz;  // Controlled_Buffer controlled_buffer_4
  assign controlled_buffer_1_out = Mul ? multiplier_1_out : 8'bz;  // Controlled_Buffer controlled_buffer_5
  Multiplier multiplier_1 (.b(DBI), .out(multiplier_1_out), .cout(multiplier_1_cout));  // open: a, cin
  assign controlled_buffer_1_out = Div ? divider_1_out : 8'bz;  // Controlled_Buffer controlled_buffer_6
  Divider divider_1 (.a(AI), .b(DBI), .out(divider_1_out));  // open: upper, rem
  and and_1 (C, multiplier_1_cout[0], multiplier_1_cout[1], multiplier_1_cout[2], multiplier_1_cout[3], multiplier_1_cout[4], multiplier_1_cout[5], multiplier_1_cout[6], multiplier_1_cout[7]);
  assign and_2_out = AI & DBI;  // AND_Gate and_2, 8 bits wide
  assign controlled_buffer_1_out = BAnd ? and_2_out : 8'bz;  // Controlled_Buffer controlled_buffer_7
  assign or_1_out = AI | DBI;  // OR_Gate or_1, 8 bits wide
  assign controlled_buffer_1_out = BOr ? or_1_out : 8'bz;  // Controlled_Buffer controlled_buffer_8
  assign xor_1_out = AI ^ DBI;  // XOR_Gate xor_1, 8 bits wide
  assign controlled_buffer_1_out = BXOr ? xor_1_out : 8'bz;  // Controlled_Buffer controlled_buffer_9
  Shifter shifter_1 (.in(AI), .\dist (DBI[2:0]), .out(shifter_1_out));
  Shifter #(.shift("lr")) shifter_2 (.in(AI), .\dist (DBI[2:0]), .out(shifter_2_out));
  assign not_1_out = ~AI;  // NOT_Gate not_1, 8 bits wide
  Adder adder_2 (.a(AI), .b({8{1'b0}}), .out(adder_2_out), .cin(1'b1));  // open: cout
  Subtractor subtractor_2 (.a(AI), .b({8{1'b0}}), .out(subtractor_2_out), .bin(1'b1));  // open: bout
  assign controlled_buffer_1_out = Shl ? shifter_1_out : 8'bz;  // Controlled_Buffer controlled_buffer_10
  assign controlled_buffer_1_out = Shr ? shifter_2_out : 8'bz;  // Controlled_Buffer controlled_buffer_11
  assign controlled_buffer_1_out = BNot ? not_1_out : 8'bz;  // Controlled_Buffer controlled_buffer_12
  assign controlled_buffer_1_out = Inc ? adder_2_out : 8'bz;  // Controlled_Buffer controlled_buffer_13
  assign controlled_buffer_1_out = Dec ? subtractor_2_out : 8'bz;  // Controlled_Buffer controlled_buffer_14
  assign DBO = OE ? controlled_buffer_1_out : 8'bz;  // Controlled_Buffer controlled_buffer_15
  nor nor_1 (Z, controlled_buffer_1_out[0], controlled_buffer_1_out[1], controlled_buffer_1_out[2], controlled_buffer_1_out[3], controlled_buffer_1_out[4], controlled_buffer_1_out[5], controlled_buffer_1_out[6], controlled_buffer_1_out[7]);
endmodule

module CSD (
  input  [7:0] Opcode,
  output PCE,
  output PCI,
  output PCO,
  output LAI,
  output LAO,
  output HAI,
  output HAO,
  output SPI,
  output SPO,
  output MEI,
  output MEO,
  output IRI,
  output ARI,
  output ARO,
  output XRI,
  output XRO,
  output YRI,
  output YRO,
  output SRI,
  output SRO,
  output RFI,
  output CFI,
  output IFS,
  output IFC,
  output HFS,
  output ZFO,
  output CFO,
  output EFO,
  output LFO,
  output GFO,
  output IFO,
  output AAD,
  output ASU,
  output AMU,
  output ADI,
  output AAN,
  output AIO,
  output AXO,
  output ASL,
  output ASR,
  output ANO,
  output AIN,
  output ADE,
  output ALO
);

  wire [47:44] rom_1_data;

  ROM #(.dataWidth(48)) rom_1 (
    .addr(Opcode),
    .data({rom_1_data, ALO, ADE, AIN, ANO, ASR, ASL, AXO, AIO, AAN, ADI, AMU, ASU, AAD, IFO, GFO, LFO, EFO, CFO, ZFO, HFS, IFC, IFS, CFI, RFI, SRO, SRI, YRO, YRI, XRO, XRI, ARO, ARI, IRI, MEO, MEI, SPO, SPI, HAO, HAI, LAO, LAI, PCO, PCI, PCE}));
endmodule

module IR (
  input  [7:0] DI,
  input  WE,
  input  Clk,
  input  Reset,
  output [7:0] DO
);

  Register register_1 (.D(DI), .en(WE), .clk(Clk), .Q(DO), .clr(Reset));
endmodule

module AR (
  input  Clk,
  input  Rst,
  input  [7:0] ADLI,
  input  [7:0] ADHI,
  input  LWE,
  input  HWE,
  output [7:0] ADLO,
  output [7:0] ADHO
);

  Register register_1 (.D(ADLI), .en(LWE), .clk(Clk), .Q(ADLO), .clr(Rst));
  Register register_2 (.D(ADHI), .en(HWE), .clk(Clk), .Q(ADHO), .clr(Rst));
endmodule

module SP (
  input  [7:0] DI,
  input  OE,
  input  WE,
  input  Clk,
  input  Reset,
  output [7:0] DO
);

  wire [7:0] register_1_q;

  Register register_1 (.D(DI), .en(WE), .clk(Clk), .Q(register_1_q), .clr(Reset));
  assign DO = OE ? register_1_q : 8'bz;  // Controlled_Buffer controlled_buffer_1
endmodule
